# Fritzing sketch watering_wires (saved by Fritzing 0.9.3b)
breadboards: 1

parts:
  Raspberry_Pi1 = Raspberry Pi 2
  5V_3A_Power_Supply = Power plug
  WeMos_D1_Mini_Relay_Shield_V1 = WeMos D1 Mini Relay Shield V2
  Wasserpumpe = DC Motor

nets:
  N1: Raspberry_Pi1.GPIO18, WeMos_D1_Mini_Relay_Shield_V1.RST
  N2: Raspberry_Pi1.GND, WeMos_D1_Mini_Relay_Shield_V1.D1
  N3: 5V_3A_Power_Supply.GND, WeMos_D1_Mini_Relay_Shield_V1.G, Wasserpumpe.pin_1
  VCC: 5V_3A_Power_Supply.VCC, WeMos_D1_Mini_Relay_Shield_V1.5V, WeMos_D1_Mini_Relay_Shield_V1.COM
  N4: WeMos_D1_Mini_Relay_Shield_V1.NO, Wasserpumpe.pin_2
